# Fritzing sketch raspberrytestsetup (saved by Fritzing 0.9.4)

parts:
  Raspberry_Pi_1 = Raspberry Pi 3 [part_number=RPI-3-V1.2]
  Q1 = TRANSISTOR_NPN [package=to-92]
  R1 = Resistor [tolerance=±5% resistance=1k package=THT]
  RJ12 = RJ12
  R2 = Resistor [tolerance=±5% resistance=1k package=THT]

nets:
  N1: Raspberry_Pi_1.3v3, R1.Pin_1
  N2: Raspberry_Pi_1.GND, Q1.E, RJ12.pin_6
  N3: Raspberry_Pi_1.GIPO15, Q1.C, R1.Pin_0
  N4: Q1.B, RJ12.pin_5, R2.Pin_1
  N5: RJ12.pin_1, RJ12.pin_2, R2.Pin_0

notes:
  Pin 1
  Pin 6
